# Fritzing sketch power (saved by Fritzing 0.9.3b)
breadboards: 1

parts:
  Bateria_1 = 18650 battery holder [package=battery-18650-kit]
  Bateria_2 = 18650 battery holder [package=battery-18650-kit]
  Driver_motoare = L298N DC motor driver
  Incarcator_1 = TP4056 [chip_label=TP4056 package="DIP (Dual Inline) [THT]"]
  Incarcator_2 = TP4056 [chip_label=TP4056 package="DIP (Dual Inline) [THT]"]
  Arduino = Arduino Mega 2560 (Rev3)
  Intrerupator_Arduino = SPST Switch [package=switch-spdt]
  Intrerupator_motoare = SPST Switch [package=switch-spdt]
  Releu_incarcare/descarcare = RELAY [package=relay-jzc]

nets:
  N1: Bateria_1.+, Incarcator_1.pin4, Intrerupator_Arduino.P, Intrerupator_motoare.P, Releu_incarcare/descarcare.NC
  N2: Bateria_1.-, Incarcator_1.pin5
  N3: Bateria_2.+, Incarcator_2.pin4
  GND: Bateria_2.-, Driver_motoare.GND, Incarcator_2.pin5, Arduino.GND, Releu_incarcare/descarcare.MAIN
  N4: Driver_motoare.12V, Intrerupator_motoare.O
  N5: Incarcator_2.pin1, Releu_incarcare/descarcare.COIL1
  N6: Incarcator_2.pin6, Releu_incarcare/descarcare.COIL2
  N7: Arduino.VIN, Intrerupator_Arduino.O

custom parts:
  18650 battery holder: 18650 Battery Holder
  L298N DC motor driver: 2x DC motor driver with 78M05 positive voltage regulator (7..35 V) L298N: max 46 V, 2 A Set 5 V Enable jumper to enable 5 V regultor (needed for the L298N) and +5 V output at screw terminal or supply external +5 V at screw terminal Set ENA and/or ENB to +5 V to enable motor permanently or supply ENA and/or ENB with PWM signal IN1 and IN2 set rotation directory for motor A (OUT1/OUT2) IN2 and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
  TP4056: A DIP stand-in part for whatever IC you want. With 6 pins on a 300mil dual inline package (DIP) footprint.
  Arduino Mega 2560 (Rev3): The Arduino Mega 2560 is a microcontroller board based on the ATmega2560 (datasheet). It has 54 digital input/output pins (of which 14 can be used as PWM outputs), 16 analog inputs, 4 UARTs (hardware serial ports), a 16 MHz crystal oscillator, a USB connection, a power jack, an ICSP header, and a reset button. It contains everything needed to support the microcontroller; simply connect it to a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
