# Fritzing sketch schema (saved by Fritzing 0.9.3b)
breadboards: 1

parts:
  GPS = NEO-6M GPS Module [part_number=GY-GPS6MV2]
  L298N = L298N DC motor driver
  L2 = DC Motor
  ESP9266 = WeMos D1 Mini
  Arduino_Mega = Arduino Mega 2560 (Rev3)
  Raspberry_Pi_3B = Raspberry Pi 3 [part_number=RPI-3-V1.2]
  Collision_Switch = Adafruit Push-button Power Switch Breakout [package=THT]
  Level_Shifter = Logic Level Converter
  L1 = DC Motor
  R1 = DC Motor
  R2 = DC Motor
  BAT1 = 18650 battery holder [package=battery-18650-kit]
  BAT2 = 18650 battery holder [package=battery-18650-kit]
  Front_Left = hc-sr04
  Voltage_Regulator = Voltage Regulator - 5V [package="TO220 [THT]"]
  Front_Right = hc-sr04

nets:
  GND: GPS.GND, L298N.GND, Arduino_Mega.GND, Raspberry_Pi_3B.GND, Collision_Switch.GND, Level_Shifter.GND, BAT2.-, Front_Left.GND, Voltage_Regulator.GND
  N1: GPS.Tx, Arduino_Mega.D19/RX1
  N2: GPS.Rx, Arduino_Mega.D18/TX1
  VCC: GPS.Vcc, L298N.12V, L298N.5V-ENA-JMP-I, L298N.5V-ENA-JMP-O, Arduino_Mega.VIN, Collision_Switch.IN, Level_Shifter.HV, BAT1.+, Voltage_Regulator.input_voltage
  N3: L298N.OUT1, L2.pin_1, L1.pin_1
  N4: L298N.OUT2, L2.pin_2, L1.pin_2
  N5: L298N.OUT3, R1.pin_2, R2.pin_2
  N6: L298N.OUT4, R1.pin_1, R2.pin_1
  N7: L298N.ENA, Arduino_Mega.D7_PWM
  N8: L298N.IN1, Arduino_Mega.D5_PWM
  N9: L298N.IN2, Arduino_Mega.D4_PWM
  N10: L298N.IN3, Arduino_Mega.D3_PWM
  N11: L298N.IN4, Arduino_Mega.D2_PWM
  N12: L298N.ENB, Arduino_Mega.D6_PWM
  N13: ESP9266.RX, Level_Shifter.RX2_LV
  N14: ESP9266.TX, Level_Shifter.TX2_LV
  N15: Arduino_Mega.D17_PWM/RX2, Collision_Switch.OUT
  N16: Arduino_Mega.D15/RX3, Level_Shifter.TX2_HV
  N17: Arduino_Mega.D14/TX3, Level_Shifter.RX2_HV
  N18: Arduino_Mega.D0_RX0, Level_Shifter.RX_HV
  N19: Arduino_Mega.D1_TX0, Level_Shifter.TX_HV
  N20: Arduino_Mega.D32, Front_Left.Echo
  N21: Arduino_Mega.D33, Front_Left.VCC
  N22: Arduino_Mega.D34, Front_Right.Echo
  N23: Arduino_Mega.D35, Front_Right.VCC
  N24: Raspberry_Pi_3B.3v3, Level_Shifter.LV
  N25: Raspberry_Pi_3B.GPIO15, Level_Shifter.TX_LV
  N26: Raspberry_Pi_3B.GPIO14, Level_Shifter.RX_LV
  N27: Raspberry_Pi_3B.5V, Voltage_Regulator.output_voltage

custom parts:
  NEO-6M GPS Module: GY-GPS6MV2 NEO-6M GPS Module Module based on U-blox NEO-6M GPS engine, incorporating regulator for 3.3-5V DC input, MS621FE-compatible rechargeable battery for backup and EEPROM for storing configuration settings. Links: NEO-6 series product information page NEO-6 Datasheet
  L298N DC motor driver: 2x DC motor driver with 78M05 positive voltage regulator (7..35 V) L298N: max 46 V, 2 A Set 5 V Enable jumper to enable 5 V regultor (needed for the L298N) and +5 V output at screw terminal or supply external +5 V at screw terminal Set ENA and/or ENB to +5 V to enable motor permanently or supply ENA and/or ENB with PWM signal IN1 and IN2 set rotation directory for motor A (OUT1/OUT2) IN2 and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
  18650 battery holder: 18650 Battery Holder
  hc-sr04: This is a HC-SR04 Distance Sensor
