# Fritzing sketch schematic (saved by Fritzing 0.9.3b)

parts:
  hc-sr1 = hc-sr04
  hc-sr2 = hc-sr04
  Part1 = Arduino Mega 2560 (Rev3)
  BAT1 = 18650 battery holder [package=battery-18650-kit]
  BAT2 = 18650 battery holder [package=battery-18650-kit]
  Mod1 = L298N DC motor driver
  Raspberry_Pi_1 = Raspberry Pi 3 [part_number=RPI-3-V1.2]
  M1 = DC Motor
  M2 = DC Motor
  M3 = DC Motor
  M4 = DC Motor
  WeMos_D1_Mini1 = WeMos D1 Mini
  M5 = NEO-6M GPS Module [part_number=GY-GPS6MV2]
  Switch1 = Switch with Pull-Up and LED

nets:
  VCC: hc-sr1.VCC, hc-sr2.VCC, Part1.5V, WeMos_D1_Mini1.5V, M5.Vcc, Switch1.VCC
  N1: hc-sr1.Trig, Part1.D33
  N2: hc-sr1.Echo, Part1.D32
  GND: hc-sr1.GND, hc-sr2.GND, Part1.GND, BAT2.-, Mod1.GND, Raspberry_Pi_1.GND, WeMos_D1_Mini1.G, M5.GND, Switch1.GND
  N3: hc-sr2.Trig, Part1.D35
  N4: hc-sr2.Echo, Part1.D34
  N5: Part1.D19/RX1, M5.Tx
  N6: Part1.D18/TX1, M5.Rx
  N7: Part1.D17_PWM/RX2, Switch1.OUT
  N8: Part1.D15/RX3, WeMos_D1_Mini1.TX
  N9: Part1.D14/TX3, WeMos_D1_Mini1.RX
  VIN: Part1.VIN, BAT1.+, Mod1.12V
  N10: Part1.D0_RX0, Raspberry_Pi_1.GPIO14
  N11: Part1.D1_TX0, Raspberry_Pi_1.GPIO18, Raspberry_Pi_1.GPIO15
  N12: Part1.D2_PWM, Mod1.IN4
  N13: Part1.D3_PWM, Mod1.IN3
  N14: Part1.D4_PWM, Mod1.IN2
  N15: Part1.D5_PWM, Mod1.IN1
  N16: Part1.D6_PWM, Mod1.ENB
  N17: Part1.D7_PWM, Mod1.ENA
  N18: BAT1.-, BAT2.+
  N19: Mod1.OUT1, M3.pin_2, M4.pin_2
  N20: Mod1.OUT2, M3.pin_1, M4.pin_1
  N21: Mod1.OUT3, M1.pin_2, M2.pin_2
  N22: Mod1.OUT4, M1.pin_1, M2.pin_1

custom parts:
  18650 battery holder: 18650 Battery Holder
  L298N DC motor driver: 2x DC motor driver with 78M05 positive voltage regulator (7..35 V) L298N: max 46 V, 2 A Set 5 V Enable jumper to enable 5 V regultor (needed for the L298N) and +5 V output at screw terminal or supply external +5 V at screw terminal Set ENA and/or ENB to +5 V to enable motor permanently or supply ENA and/or ENB with PWM signal IN1 and IN2 set rotation directory for motor A (OUT1/OUT2) IN2 and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
  NEO-6M GPS Module: GY-GPS6MV2 NEO-6M GPS Module Module based on U-blox NEO-6M GPS engine, incorporating regulator for 3.3-5V DC input, MS621FE-compatible rechargeable battery for backup and EEPROM for storing configuration settings. Links: NEO-6 series product information page NEO-6 Datasheet
